// Logisim project OneBit.circ as structural Verilog: 25 circuits, main circuit main
module main (
  input  _2,
  input  _1,
  input  _0,
  input  Data,
  input  Reset,
  input  Clock
);

  wire A_2_data, A_2_write_data, alu_1_p, alu_1_s, alu_1_write_data, B, B_2_data, B_2_write_data, C_data,
       C_write_data, decoderopt_new_1_a_read_enable, decoderopt_new_1_ab_write_enable,
       decoderopt_new_1_alu_read_enable, decoderopt_new_1_alu_s_p, decoderopt_new_1_b_read_enable,
       decoderopt_new_1_bus_data, decoderopt_new_1_c_read_enable, decoderopt_new_1_c_write_enable,
       decoderopt_new_1_ram_address, decoderopt_new_1_ram_read_enable, decoderopt_new_1_ram_write_enable,
       ram_new2_1_data_0, ram_new2_1_data_1, ram_new2_1_write_data;

  DecoderOpt__new decoderopt_new_1 (
    .Data(Data), ._2(_2), ._1(_1), ._0(_0), .A_Read_Enable(decoderopt_new_1_a_read_enable),
    .B_Read_Enable(decoderopt_new_1_b_read_enable), .AB_Write_Enable(decoderopt_new_1_ab_write_enable),
    .C_Read_Enable(decoderopt_new_1_c_read_enable), .C_Write_Enable(decoderopt_new_1_c_write_enable),
    .Alu_Read_Enable(decoderopt_new_1_alu_read_enable), .Alu_S_P(decoderopt_new_1_alu_s_p),
    .Ram_Read_Enable(decoderopt_new_1_ram_read_enable), .Ram_Write_Enable(decoderopt_new_1_ram_write_enable),
    .Ram_Address(decoderopt_new_1_ram_address), .Bus_Data(decoderopt_new_1_bus_data));
  // Probe on decoderopt_new_1_ram_read_enable
  // Probe on B
  // Probe on decoderopt_new_1_ram_write_enable
  Ram__new2 ram_new2_1 (
    .Clock(Clock), .Read_Enable(decoderopt_new_1_ram_read_enable), .Read_Data(B),
    .Write_Enable(decoderopt_new_1_ram_write_enable), .Write_Data(ram_new2_1_write_data),
    .Address(decoderopt_new_1_ram_address), .Reset(Reset), .C_Data_Input(C_write_data),
    .Decoder_Data_Input(decoderopt_new_1_bus_data), .Alu_Data_Input(alu_1_write_data),
    .Data_0(ram_new2_1_data_0), .Data_1(ram_new2_1_data_1), .Output_Bus_Data(B));
  // Probe on ram_new2_1_write_data
  // Probe on decoderopt_new_1_ram_address
  // Probe on ram_new2_1_data_0
  // Probe on ram_new2_1_data_1
  // Probe on B
  ALU alu_1 (
    .A(A_2_write_data), .B(B_2_write_data), .Write_Enable(decoderopt_new_1_alu_read_enable),
    .Write_Data(alu_1_write_data), .S_P(decoderopt_new_1_alu_s_p), .S(alu_1_s), .P(alu_1_p));
  // Probe on A_2_write_data
  // Probe on B_2_write_data
  // Probe on alu_1_s
  // Probe on alu_1_p
  // Probe on decoderopt_new_1_alu_s_p
  // Probe on decoderopt_new_1_alu_read_enable
  // Probe on alu_1_write_data
  Register__new A_2 (
    .Clock(Clock), .Read_Enable(decoderopt_new_1_a_read_enable), .Read_Data(B),
    .Write_Enable(decoderopt_new_1_ab_write_enable), .Write_Data(A_2_write_data), .Reset(Reset),
    .Data(A_2_data));
  Register__new B_2 (
    .Clock(Clock), .Read_Enable(decoderopt_new_1_b_read_enable), .Read_Data(B),
    .Write_Enable(decoderopt_new_1_ab_write_enable), .Write_Data(B_2_write_data), .Reset(Reset),
    .Data(B_2_data));
  Register__new C (
    .Clock(Clock), .Read_Enable(decoderopt_new_1_c_read_enable), .Read_Data(B),
    .Write_Enable(decoderopt_new_1_c_write_enable), .Write_Data(C_write_data), .Reset(Reset), .Data(C_data));
  // Probe on decoderopt_new_1_a_read_enable
  // Probe on B
  // Probe on decoderopt_new_1_ab_write_enable
  // Probe on A_2_write_data
  // Probe on A_2_data
  // Probe on decoderopt_new_1_b_read_enable
  // Probe on B
  // Probe on decoderopt_new_1_ab_write_enable
  // Probe on B_2_write_data
  // Probe on B_2_data
  // Probe on decoderopt_new_1_c_read_enable
  // Probe on B
  // Probe on decoderopt_new_1_c_write_enable
  // Probe on C_write_data
  // Probe on C_data

  // Other names for the same wires on the sheet: C = Clock; R = Reset

  // Notes on the sheet:
  //   [000] Nop
  //   [001] Rom->A (Data)
  //   [010] Rom->B (Data) 
  //   [011] Rom->C (Data)
  //   [100] Add->C (S\P)
  //   [101] C->AB (A\B)
  //   [110] Ram->C (Address)
  //   [111] C->Ram (Address)
endmodule

module Register (
  input  Clock,
  input  Read,
  input  Read_Data,
  input  Write,
  input  Reset,
  output Memory,
  output Write_Data
);

  wire nand_1_out, nand_2_out, nand_3_out, nand_4_out, nand_6_out, not_1_out, not_3_out, not_4_out;

  nand nand_1 (nand_1_out, Clock, Read);
  not not_1 (not_1_out, nand_1_out);
  nand nand_2 (nand_2_out, Memory, Write);
  not not_2 (Write_Data, nand_2_out);
  not not_3 (not_3_out, Read_Data);
  nand nand_3 (nand_3_out, Read_Data, not_1_out);
  nand nand_4 (nand_4_out, not_1_out, not_3_out);
  not not_4 (not_4_out, Reset);
  nand nand_5 (Memory, nand_3_out, nand_6_out);
  nand nand_6 (nand_6_out, Memory, not_4_out, nand_4_out);
  // Probe on Memory
  // Probe on nand_6_out

  // Notes on the sheet:
  //   Q
  //   NQ
endmodule

module Ram (
  input  Read_Enable,
  input  Read_Data,
  input  Write_Enable,
  input  Address,
  output Data_0,
  output Data_1,
  output Write_Data
);

  wire Cell_0_write_data, Cell_1_write_data, nor_1_out, nor_2_out, nor_3_out, nor_4_out, not_1_out,
       not_2_out, not_3_out;

  nand nand_1 (Write_Data, Cell_0_write_data, Cell_1_write_data);
  not not_1 (not_1_out, Write_Enable);
  nor nor_1 (nor_1_out, not_3_out, not_1_out);
  nor nor_2 (nor_2_out, not_1_out, Address);
  RegisterInvert Cell_0 (
    .Read(nor_4_out), .Read_Data(Read_Data), .Write(nor_2_out), .Write_Data(Cell_0_write_data),
    .Memory(Data_0));
  RegisterInvert Cell_1 (
    .Read(nor_3_out), .Read_Data(Read_Data), .Write(nor_1_out), .Write_Data(Cell_1_write_data),
    .Memory(Data_1));
  not not_2 (not_2_out, Read_Enable);
  not not_3 (not_3_out, Address);
  nor nor_3 (nor_3_out, not_3_out, not_2_out);
  nor nor_4 (nor_4_out, not_2_out, Address);
endmodule

module Decoder_3_8 (
  input  _0,
  input  _1,
  input  _2,
  output _0_2,
  output _1_2,
  output _2_2,
  output _3,
  output _4,
  output _5,
  output _6,
  output _7
);

  wire not_1_out, not_2_out, not_3_out;

  not not_1 (not_1_out, _0);
  not not_2 (not_2_out, _1);
  not not_3 (not_3_out, _2);
  and and_1 (_0_2, not_1_out, not_2_out, not_3_out);
  and and_2 (_1_2, _0, not_2_out, not_3_out);
  and and_3 (_2_2, not_1_out, not_3_out, _1);
  and and_4 (_3, not_3_out, _0, _1);
  and and_5 (_4, not_1_out, not_2_out, _2);
  and and_6 (_5, not_2_out, _0, _2);
  and and_7 (_6, not_1_out, _1, _2);
  and and_8 (_7, _0, _1, _2);
endmodule

module D_Trigger (
  input  D,
  input  C,
  output Q,
  output NQ
);

  wire nand_1_out, nand_2_out, not_1_out;

  not not_1 (not_1_out, D);
  nand nand_1 (nand_1_out, D, C);
  nand nand_2 (nand_2_out, C, not_1_out);
  SR_Trigger sr_trigger_1 (.S(nand_1_out), .R(nand_2_out), .Q(NQ), .NQ(Q));
endmodule

module T_Trigger (
  input  T,
  output Q
);

  wire d_trigger_1_nq, d_trigger_2_q, not_1_out;

  D_Trigger d_trigger_1 (.D(d_trigger_2_q), .C(T), .NQ(d_trigger_1_nq));  // open: Q
  not not_1 (not_1_out, T);
  D_Trigger d_trigger_2 (.D(d_trigger_1_nq), .C(not_1_out), .Q(d_trigger_2_q), .NQ(Q));
endmodule

module SR_Trigger (
  input  S,
  input  R,
  output Q,
  output NQ
);

  S_R_Flip_Flop #(.trigger("high")) s_r_ff_1 (.S(S), .clk(1'b1), .R(R), .Q(Q), .Qn(NQ));  // open: preset, reset, en
endmodule

module Rom (
  input  in_1
);

  wire decoder_3_8_1__0_2, decoder_3_8_1__1_2, decoder_3_8_1__2_2, decoder_3_8_1__3, decoder_3_8_1__4,
       decoder_3_8_1__5, decoder_3_8_1__6, decoder_3_8_1__7, t_trigger_1_q, t_trigger_2_q, t_trigger_3_q;

  T_Trigger t_trigger_1 (.T(t_trigger_2_q), .Q(t_trigger_1_q));
  T_Trigger t_trigger_2 (.T(in_1), .Q(t_trigger_2_q));
  T_Trigger t_trigger_3 (.T(t_trigger_1_q), .Q(t_trigger_3_q));
  Decoder_3_8 decoder_3_8_1 (
    ._0(t_trigger_2_q), ._1(t_trigger_1_q), ._2(t_trigger_3_q), ._0_2(decoder_3_8_1__0_2),
    ._1_2(decoder_3_8_1__1_2), ._2_2(decoder_3_8_1__2_2), ._3(decoder_3_8_1__3), ._4(decoder_3_8_1__4),
    ._5(decoder_3_8_1__5), ._6(decoder_3_8_1__6), ._7(decoder_3_8_1__7));
endmodule

module Decoder (
  input  _2,
  input  _1,
  input  _0,
  input  Data,
  input  Clock,
  output A_Read,
  output A_Write,
  output X_Read,
  output Y_Read,
  output Sum_Write,
  output Sum_Result,
  output Ram_Read,
  output Ram_Write,
  output Ram_Address,
  output Bus
);

  wire and_1_out, and_2_out, decoder_3_8_1__0_2, decoder_3_8_1__1_2, decoder_3_8_1__2_2, decoder_3_8_1__3,
       decoder_3_8_1__5, decoder_3_8_1__7, not_1_out, or_1_out, or_3_out, or_4_out, or_5_out, or_6_out;

  Decoder_3_8 decoder_3_8_1 (
    ._0(_0), ._1(_1), ._2(_2), ._0_2(decoder_3_8_1__0_2), ._1_2(decoder_3_8_1__1_2),
    ._2_2(decoder_3_8_1__2_2), ._3(decoder_3_8_1__3), ._4(Sum_Write), ._5(decoder_3_8_1__5), ._6(Ram_Write),
    ._7(decoder_3_8_1__7));
  not not_1 (not_1_out, Data);
  or or_1 (or_1_out, decoder_3_8_1__7, Ram_Write);
  and and_1 (and_1_out, Data, decoder_3_8_1__5);
  and and_2 (and_2_out, decoder_3_8_1__5, not_1_out);
  and and_3 (Ram_Address, or_1_out, Data);
  or or_2 (A_Write, decoder_3_8_1__5, decoder_3_8_1__7);
  or or_3 (or_3_out, decoder_3_8_1__1_2, decoder_3_8_1__2_2, decoder_3_8_1__3);
  and and_4 (Bus, or_3_out, Data);
  and and_5 (Sum_Result, Sum_Write, Data);
  or or_4 (or_4_out, decoder_3_8_1__1_2, Sum_Write, Ram_Write);
  or or_5 (or_5_out, decoder_3_8_1__2_2, and_1_out);
  or or_6 (or_6_out, decoder_3_8_1__3, and_2_out);
  and and_6 (A_Read, Clock, or_4_out);
  and and_7 (X_Read, Clock, or_5_out);
  and and_8 (Y_Read, Clock, or_6_out);
  and and_9 (Ram_Read, Clock, decoder_3_8_1__7);

  // Notes on the sheet:
  //   Nop
  //   Rom-A (Const)
  //   Rom-X (Const)
  //   Rom-Y (Const)
  //   Sum (Result)
  //   A-XY (X-Y)
  //   Ram-A (Address)
  //   A-Ram (Address)
endmodule

module HS (
  input  A,
  input  B,
  output S,
  output P
);

  wire nand_1_out, nand_2_out, nand_3_out;

  nand nand_1 (nand_1_out, A, B);
  nand nand_2 (nand_2_out, A, nand_1_out);
  nand nand_3 (nand_3_out, nand_1_out, B);
  not not_1 (P, nand_1_out);
  nand nand_4 (S, nand_2_out, nand_3_out);
endmodule

// Mux
module Multiplexer_2_1 (
  input  _0,
  input  _1,
  input  Address,
  output Q
);

  wire nand_1_out, nand_2_out, not_1_out;

  not not_1 (not_1_out, Address);
  nand nand_1 (nand_1_out, _0, not_1_out);
  nand nand_2 (nand_2_out, _1, Address);
  nand nand_3 (Q, nand_1_out, nand_2_out);
endmodule

module RegisterAlwaysWrite (
  input  Read,
  input  Read_Data,
  output Memory,
  output Write_Data
);

  wire nand_1_out, nand_2_out, nand_3_out, nand_4_out, not_1_out;

  nand nand_1 (nand_1_out, Read, Read_Data);
  not not_1 (not_1_out, nand_1_out);
  nand nand_2 (nand_2_out, nand_1_out, Read);
  nand nand_3 (nand_3_out, Read, not_1_out);
  nand nand_4 (nand_4_out, nand_2_out, Memory);
  nand nand_5 (Memory, nand_4_out, nand_3_out);

  assign Write_Data = Memory;
endmodule

module RegisterInvert (
  input  Read,
  input  Read_Data,
  input  Write,
  output Memory,
  output Write_Data
);

  wire nand_1_out, nand_3_out, nand_4_out, nand_5_out, not_1_out;

  nand nand_1 (nand_1_out, Read, Read_Data);
  nand nand_2 (Write_Data, Memory, Write);
  not not_1 (not_1_out, nand_1_out);
  nand nand_3 (nand_3_out, nand_1_out, Read);
  nand nand_4 (nand_4_out, Read, not_1_out);
  nand nand_5 (nand_5_out, nand_3_out, Memory);
  nand nand_6 (Memory, nand_5_out, nand_4_out);
endmodule

module DecoderOpt (
  input  _2,
  input  _1,
  input  _0,
  input  Data,
  input  Clock,
  output A_Read,
  output A_Write,
  output X_Read,
  output Y_Read,
  output Sum_Write,
  output Sum_Result,
  output Ram_Read,
  output Ram_Write,
  output Ram_Address,
  output Bus
);

  wire decoder_3_8_invert_1__0_2, decoder_3_8_invert_1__1_2, decoder_3_8_invert_1__2_2,
       decoder_3_8_invert_1__3, decoder_3_8_invert_1__4, decoder_3_8_invert_1__5, decoder_3_8_invert_1__6,
       decoder_3_8_invert_1__7, nor_1_out, nor_2_out, nor_3_out, nor_5_out, nor_6_out, nor_7_out, nor_8_out,
       not_2_out, not_3_out, not_4_out, not_5_out, not_6_out, not_8_out;

  // NOT_Gate not_1 has open pins: in=decoder_3_8_invert_1__0_2, out=open
  Decoder_3_8_Invert decoder_3_8_invert_1 (
    ._0(_0), ._1(_1), ._2(_2), ._0_2(decoder_3_8_invert_1__0_2), ._1_2(decoder_3_8_invert_1__1_2),
    ._2_2(decoder_3_8_invert_1__2_2), ._3(decoder_3_8_invert_1__3), ._4(decoder_3_8_invert_1__4),
    ._5(decoder_3_8_invert_1__5), ._6(decoder_3_8_invert_1__6), ._7(decoder_3_8_invert_1__7));
  not not_2 (not_2_out, Clock);
  not not_3 (not_3_out, decoder_3_8_invert_1__1_2);
  not not_4 (not_4_out, decoder_3_8_invert_1__2_2);
  not not_5 (not_5_out, decoder_3_8_invert_1__3);
  not not_6 (not_6_out, Data);
  not not_7 (Ram_Write, decoder_3_8_invert_1__6);
  nor nor_1 (nor_1_out, not_6_out, decoder_3_8_invert_1__5);
  nor nor_2 (nor_2_out, decoder_3_8_invert_1__5, Data);
  nand nand_1 (A_Write, decoder_3_8_invert_1__5, decoder_3_8_invert_1__7);
  nor nor_3 (nor_3_out, not_3_out, not_4_out, not_5_out);
  nor nor_4 (Bus, nor_3_out, not_6_out);
  not not_8 (not_8_out, decoder_3_8_invert_1__7);
  nor nor_5 (nor_5_out, not_5_out, nor_1_out);
  not not_9 (Sum_Write, decoder_3_8_invert_1__4);
  nor nor_6 (nor_6_out, not_8_out, Ram_Write);
  nor nor_7 (nor_7_out, Ram_Write, not_3_out, Sum_Write);
  nor nor_8 (nor_8_out, not_4_out, nor_2_out);
  nor nor_9 (A_Read, not_2_out, nor_7_out);
  nor nor_10 (X_Read, not_2_out, nor_8_out);
  nor nor_11 (Y_Read, not_2_out, nor_5_out);
  nor nor_12 (Sum_Result, decoder_3_8_invert_1__4, not_6_out);
  nor nor_13 (Ram_Read, not_2_out, decoder_3_8_invert_1__7);
  nor nor_14 (Ram_Address, nor_6_out, not_6_out);

  // Notes on the sheet:
  //   [000] Nop
  //   [001] Rom-A (Const)
  //   [010] Rom-X (Const) 
  //   [011] Rom-Y (Const)
  //   [100] Sum (Result)
  //   [101] A-XY (X-Y)
  //   [110] Ram-A (Address)
  //   [111] A-Ram (Address)
endmodule

module Decoder_3_8_Invert (
  input  _0,
  input  _1,
  input  _2,
  output _0_2,
  output _1_2,
  output _2_2,
  output _3,
  output _4,
  output _5,
  output _6,
  output _7
);

  wire not_1_out, not_2_out, not_3_out;

  not not_1 (not_1_out, _0);
  not not_2 (not_2_out, _1);
  not not_3 (not_3_out, _2);
  nand nand_1 (_0_2, not_1_out, not_2_out, not_3_out);
  nand nand_2 (_1_2, _0, not_2_out, not_3_out);
  nand nand_3 (_2_2, not_1_out, not_3_out, _1);
  nand nand_4 (_3, not_3_out, _0, _1);
  nand nand_5 (_4, not_1_out, not_2_out, _2);
  nand nand_6 (_5, not_2_out, _0, _2);
  nand nand_7 (_6, not_1_out, _1, _2);
  nand nand_8 (_7, _0, _1, _2);
endmodule

module D_Trigger__new (
  input  C,
  input  D,
  input  R,
  output Q,
  output NQ
);

  wire nand_1_out, nand_2_out, not_1_out, not_2_out;

  not not_1 (not_1_out, D);
  not not_2 (not_2_out, R);
  nand nand_1 (nand_1_out, D, C);
  nand nand_2 (nand_2_out, C, not_1_out);
  nand nand_3 (Q, nand_1_out, NQ);
  nand nand_4 (NQ, Q, nand_2_out, not_2_out);
endmodule

// Register
module Register__new (
  input  Clock,
  input  Read_Enable,
  input  Read_Data,
  input  Write_Enable,
  input  Reset,
  output Data,
  output Write_Data
);

  wire d_trigger_new_1_nq, nand_1_out, nor_1_out, not_1_out, not_2_out;

  not not_1 (not_1_out, Clock);
  not not_2 (not_2_out, Read_Enable);
  nor nor_1 (nor_1_out, not_1_out, not_2_out);
  nand nand_1 (nand_1_out, Data, Write_Enable);
  not not_3 (Write_Data, nand_1_out);
  D_Trigger__new d_trigger_new_1 (.C(nor_1_out), .D(Read_Data), .R(Reset), .Q(Data), .NQ(d_trigger_new_1_nq));

  // Notes on the sheet:
  //   Входы делаем с инверторов, потому что на них нужно вешать светодиоды
endmodule

// Ram
module Ram__new (
  input  Clock,
  input  Read_Enable,
  input  Read_Data,
  input  Write_Enable,
  input  Address,
  input  Reset,
  output Data_0,
  output Data_1,
  output Write_Data
);

  wire Cell_0_write_data, Cell_1_write_data, demux_1_output_0, demux_1_output_1, demux_2_output_0,
       demux_2_output_1, nor_1_out;

  nor nor_1 (nor_1_out, Cell_0_write_data, Cell_1_write_data);
  not not_1 (Write_Data, nor_1_out);
  Demux demux_1 (.Input(Write_Enable), .Address(Address), .Output_0(demux_1_output_0), .Output_1(demux_1_output_1));
  Demux demux_2 (.Input(Read_Enable), .Address(Address), .Output_0(demux_2_output_0), .Output_1(demux_2_output_1));
  Register__new Cell_0 (
    .Clock(Clock), .Read_Enable(demux_2_output_0), .Read_Data(Read_Data), .Write_Enable(demux_1_output_0),
    .Write_Data(Cell_0_write_data), .Reset(Reset), .Data(Data_0));
  Register__new Cell_1 (
    .Clock(Clock), .Read_Enable(demux_2_output_1), .Read_Data(Read_Data), .Write_Enable(demux_1_output_1),
    .Write_Data(Cell_1_write_data), .Reset(Reset), .Data(Data_1));
endmodule

module Demux (
  input  Input,
  input  Address,
  output Output_0,
  output Output_1
);

  wire not_1_out, not_2_out;

  not not_1 (not_1_out, Address);
  not not_2 (not_2_out, Input);
  nor nor_1 (Output_0, Address, not_2_out);
  nor nor_2 (Output_1, not_2_out, not_1_out);
endmodule

// Decoder
module DecoderOpt__new (
  input  _2,
  input  _1,
  input  _0,
  input  Data,
  output A_Read_Enable,
  output B_Read_Enable,
  output AB_Write_Enable,
  output C_Read_Enable,
  output C_Write_Enable,
  output Alu_Read_Enable,
  output Alu_S_P,
  output Ram_Read_Enable,
  output Ram_Write_Enable,
  output Ram_Address,
  output Bus_Data
);

  wire decoder_3_8_invert_1__1_2, decoder_3_8_invert_1__2_2, decoder_3_8_invert_1__3,
       decoder_3_8_invert_1__4, decoder_3_8_invert_1__5, decoder_3_8_invert_1__6, decoder_3_8_invert_1__7,
       nand_1_out, nand_2_out, nor_1_out, nor_2_out, not_1_out, not_2_out, not_3_out, not_5_out, not_8_out;

  Decoder_3_8_Invert decoder_3_8_invert_1 (
    ._0(_0), ._1(_1), ._2(_2), ._1_2(decoder_3_8_invert_1__1_2), ._2_2(decoder_3_8_invert_1__2_2),
    ._3(decoder_3_8_invert_1__3), ._4(decoder_3_8_invert_1__4), ._5(decoder_3_8_invert_1__5),
    ._6(decoder_3_8_invert_1__6), ._7(decoder_3_8_invert_1__7));  // open: _0_2
  not not_1 (not_1_out, decoder_3_8_invert_1__1_2);
  not not_2 (not_2_out, decoder_3_8_invert_1__2_2);
  not not_3 (not_3_out, decoder_3_8_invert_1__3);
  not not_4 (AB_Write_Enable, decoder_3_8_invert_1__4);
  not not_5 (not_5_out, decoder_3_8_invert_1__5);
  not not_6 (Ram_Write_Enable, decoder_3_8_invert_1__6);
  not not_7 (Ram_Read_Enable, decoder_3_8_invert_1__7);
  not not_8 (not_8_out, Data);
  nand nand_1 (nand_1_out, not_8_out, not_5_out);
  nand nand_2 (nand_2_out, not_5_out, Data);
  nor nor_1 (nor_1_out, Ram_Write_Enable, Ram_Read_Enable);
  nor nor_2 (nor_2_out, not_1_out, not_2_out, not_3_out);
  nand nand_3 (A_Read_Enable, nand_1_out, decoder_3_8_invert_1__1_2);
  nand nand_4 (B_Read_Enable, nand_2_out, decoder_3_8_invert_1__2_2);
  nand nand_5 (C_Read_Enable, decoder_3_8_invert_1__6, decoder_3_8_invert_1__4, decoder_3_8_invert_1__3);
  nand nand_6 (C_Write_Enable, decoder_3_8_invert_1__7, decoder_3_8_invert_1__5);
  nor nor_3 (Alu_S_P, decoder_3_8_invert_1__4, not_8_out);
  nor nor_4 (Ram_Address, nor_1_out, not_8_out);
  nor nor_5 (Bus_Data, nor_2_out, not_8_out);

  assign Alu_Read_Enable = AB_Write_Enable;

  // Notes on the sheet:
  //   1        2        3       4        5        6       7
  //   1        2        3       4        5        6       7
  //   Не обязательно!!!
  //   Не обязательно!!!
  //   Не обязательно!!!
  //   [000] Nop
  //   [001] Rom->A (Data)
  //   [010] Rom->B (Data) 
  //   [011] Rom->C (Data)
  //   [100] Add->C (S\P)
  //   [101] C->AB (A\B)
  //   [110] Ram->C (Address)
  //   [111] C->Ram (Address)
endmodule

// Alu
module ALU (
  input  A,
  input  B,
  input  Write_Enable,
  input  S_P,
  output S,
  output P,
  output Write_Data
);

  wire multiplexer_2_1_1_q, nand_1_out;

  not not_1 (Write_Data, nand_1_out);
  nand nand_1 (nand_1_out, multiplexer_2_1_1_q, Write_Enable);
  HS hs_1 (.A(A), .B(B), .S(S), .P(P));
  Multiplexer_2_1 multiplexer_2_1_1 (._0(S), ._1(P), .Address(S_P), .Q(multiplexer_2_1_1_q));
endmodule

module Bus (
  input  Input,
  input  Input_2,
  input  Input_3,
  input  Input_4,
  output Output
);

  wire nor_1_out;

  nor nor_1 (nor_1_out, Input, Input_2, Input_3, Input_4);
  not not_1 (Output, nor_1_out);
endmodule

module Demux2 (
  input  Input,
  input  Address,
  output Output_0,
  output Output_1
);

  wire nand_1_out, nand_2_out, not_1_out;

  not not_1 (not_1_out, Address);
  nand nand_1 (nand_1_out, not_1_out, Input);
  nand nand_2 (nand_2_out, Input, Address);
  not not_2 (Output_0, nand_1_out);
  not not_3 (Output_1, nand_2_out);
endmodule

module Decoder_2_4_Test (
  input  _0,
  input  _1,
  output _0_2,
  output _1_2,
  output _2,
  output _3
);

  wire not_1_out, not_2_out;

  not not_1 (not_1_out, _0);
  not not_2 (not_2_out, _1);
  nand nand_1 (_0_2, not_1_out, not_2_out);
  nand nand_2 (_1_2, not_2_out, _0);
  nand nand_3 (_2, not_1_out, _1);
  nand nand_4 (_3, _1, _0);
endmodule

// Ram + Bus
module Ram__new2 (
  input  Clock,
  input  Read_Enable,
  input  Read_Data,
  input  Write_Enable,
  input  Address,
  input  Reset,
  input  C_Data_Input,
  input  Decoder_Data_Input,
  input  Alu_Data_Input,
  output Data_0,
  output Data_1,
  output Write_Data,
  output Output_Bus_Data
);

  wire Cell_0_write_data, Cell_1_write_data, demux_1_output_0, demux_1_output_1, demux_2_output_0,
       demux_2_output_1, nor_1_out;

  Demux demux_1 (.Input(Write_Enable), .Address(Address), .Output_0(demux_1_output_0), .Output_1(demux_1_output_1));
  nor nor_1 (nor_1_out, Cell_1_write_data, Cell_0_write_data, C_Data_Input, Decoder_Data_Input, Alu_Data_Input);
  Demux demux_2 (.Input(Read_Enable), .Address(Address), .Output_0(demux_2_output_0), .Output_1(demux_2_output_1));
  not not_1 (Output_Bus_Data, nor_1_out);
  Register__new Cell_0 (
    .Clock(Clock), .Read_Enable(demux_2_output_0), .Read_Data(Read_Data), .Write_Enable(demux_1_output_0),
    .Write_Data(Cell_0_write_data), .Reset(Reset), .Data(Data_0));
  Register__new Cell_1 (
    .Clock(Clock), .Read_Enable(demux_2_output_1), .Read_Data(Read_Data), .Write_Enable(demux_1_output_1),
    .Write_Data(Cell_1_write_data), .Reset(Reset), .Data(Data_1));

  assign Write_Data = Output_Bus_Data;
endmodule
