// Logisim project Test1.circ as structural Verilog: 1 circuit, main circuit main
module main (
);

  wire transistor_1_out, undriven;

  Clock clock_1 ();  // open: out
  Transistor #(.\type ("n")) transistor_1 (.in(1'b0), .out(transistor_1_out), .gate(undriven));
  LED led_1 (.in(transistor_1_out));
  // also tied to VCC on the sheet: transistor_1_out
endmodule
